// Logisim project decod mux.circ as structural Verilog: 1 circuit, main circuit main
module main (
  input  in_1,
  input  [1:0] in_2
);

  wire decoder_1_out0, decoder_1_out1, decoder_1_out2, decoder_1_out3, undriven_4;
  wire [1:0] multiplexer_1_out, undriven, undriven_2;
  wire [3:0] undriven_3;

  Decoder #(.select(2)) decoder_1 (
    .out0(decoder_1_out0), .out1(decoder_1_out1), .out2(decoder_1_out2), .out3(decoder_1_out3), .sel(in_2));  // open: en
  Multiplexer #(.select(4), .width(2)) multiplexer_1 (
    .in5(undriven_2), .in7(undriven), .out(multiplexer_1_out), .sel(undriven_3), .en(undriven_4));  // open: in0, in1, in2, in3, in4, in6, in8, in9, in10, in11, in12, in13, in14, in15
endmodule
