// Logisim project ej1.circ as structural Verilog: 1 circuit, main circuit main
module main (
  input  [3:0] in_1,
  input  [3:0] in_2,
  input  in_3
);

  wire _1x1x_out, _11xx_out, adder_1_cout;
  wire [2:2] or_1_out;
  wire [3:0] adder_1_out, adder_2_out;

  Hex_Digit_Display hex_digit_display_1 (.value(in_1));  // open: dp
  Hex_Digit_Display hex_digit_display_2 (.value(in_2));  // open: dp
  or or_1 (or_1_out[2], _11xx_out, adder_1_cout, _1x1x_out);
  and _11xx (_11xx_out, adder_1_out[3], adder_1_out[2]);
  and _1x1x (_1x1x_out, adder_1_out[3], adder_1_out[1]);
  Adder #(.width(4)) adder_1 (.a(in_1), .b(in_2), .out(adder_1_out), .cout(adder_1_cout));  // open: cin
  Adder #(.width(4)) adder_2 (
    .a(adder_1_out), .b({in_3, {2{or_1_out[2]}}, in_3}), .out(adder_2_out));  // open: cin, cout
  Hex_Digit_Display hex_digit_display_3 (.value({{3{in_3}}, or_1_out[2]}));  // open: dp
  Hex_Digit_Display hex_digit_display_4 (.value(adder_2_out));  // open: dp

  // Notes on the sheet:
  //   control
endmodule
