// Logisim project ej2.circ as structural Verilog: 1 circuit, main circuit main
module main (
  input  [3:0] A,
  input  [3:0] B,
  input  ns___r,
  output [3:0] out_4
);

  wire [3:0] xor_1_out;

  Hex_Digit_Display hex_digit_display_1 (.value(B));  // open: dp
  Hex_Digit_Display hex_digit_display_2 (.value(A));  // open: dp
  assign xor_1_out = B ^ {4{ns___r}};  // XOR_Gate xor_1, 4 bits wide
  Adder #(.width(4)) adder_1 (.a(A), .b(xor_1_out), .out(out_4), .cin(ns___r));  // open: cout
  Hex_Digit_Display hex_digit_display_3 (.value(out_4));  // open: dp
endmodule
