// Logisim project ej3.circ as structural Verilog: 1 circuit, main circuit main
module main (
  input  [3:0] A,
  input  in_2,
  input  [1:0] B,
  input  in_4,
  output [5:0] R
);

  wire [3:0] and_2_out;
  wire [3:1] and_1_out;

  Hex_Digit_Display hex_digit_display_1 (.value(A));  // open: dp
  Hex_Digit_Display hex_digit_display_2 (.value({{2{in_4}}, B}));  // open: dp
  assign {and_1_out, R[0]} = A & {4{B[0]}};  // AND_Gate and_1, 4 bits wide
  assign and_2_out = A & {4{B[1]}};  // AND_Gate and_2, 4 bits wide
  Adder #(.width(4)) adder_1 (.a({in_2, and_1_out}), .b(and_2_out), .out(R[4:1]), .cout(R[5]));  // open: cin
endmodule
