// Logisim project ej5.circ as structural Verilog: 1 circuit, main circuit main
module main (
  input  A,
  input  B,
  input  C,
  input  D,
  input  E
);

  wire multiplexer_1_out;

  LED L (.in(multiplexer_1_out));
  Multiplexer #(.select(4)) multiplexer_1 (
    .in0(1'b0), .in1(1'b0), .in2(A), .in3(1'b1), .in4(1'b0), .in5(A), .in6(A), .in7(1'b1), .in8(1'b0),
    .in9(A), .in10(A), .in11(1'b1), .in12(1'b0), .in13(A), .in14(1'b1), .in15(1'b1), .out(multiplexer_1_out),
    .sel({B, C, D, E}));  // open: en
endmodule
