// Logisim project ej6.circ as structural Verilog: 1 circuit, main circuit main
module main (
  input  [1:0] A,
  input  [1:0] B,
  input  [1:0] G
);

  wire [0:0] adder_1_cout, and_1_out;
  wire [1:0] adder_1_out, adder_2_out, divider_1_out, divider_1_rem, multiplexer_1_out;

  Hex_Digit_Display hex_digit_display_1 (.value({2'b00, A}));  // open: dp
  Hex_Digit_Display hex_digit_display_2 (.value({2'b00, B}));  // open: dp
  and and_1 (and_1_out[0], divider_1_rem[0], G[0], G[1]);
  Adder #(.width(2)) adder_1 (.a(A), .b(B), .out(adder_1_out), .cout(adder_1_cout[0]));  // open: cin
  Divider #(.width(2)) divider_1 (
    .a(adder_1_out), .b(2'b10), .out(divider_1_out), .upper({1'b0, adder_1_cout[0]}), .rem(divider_1_rem));
  Adder #(.width(2)) adder_2 (.a(divider_1_out), .b({1'b0, and_1_out[0]}), .out(adder_2_out));  // open: cin, cout
  Multiplexer #(.select(2), .width(2)) multiplexer_1 (
    .in0(adder_2_out), .in1(A), .in2(B), .in3(adder_2_out), .out(multiplexer_1_out), .sel(G));  // open: en
  Hex_Digit_Display hex_digit_display_3 (.value({2'b00, multiplexer_1_out}));  // open: dp

  // Notes on the sheet:
  //   A
  //   B
endmodule
