// Logisim project ej2.circ as structural Verilog: 1 circuit, main circuit main
module main (
  input  C,
  input  S,
  input  Clk,
  input  R,
  input  P,
  output Q,
  output nQ
);

  wire nand_1_out, nand_2_out, nand_3_out, nand_4_out, not_1_out, not_2_out;

  nand nand_1 (nand_1_out, S, S, Clk);
  nand nand_2 (nand_2_out, Clk, R, R);
  not not_1 (not_1_out, C);
  and and_1 (Q, not_1_out, nand_3_out);
  nand nand_3 (nand_3_out, nand_1_out, nand_1_out, nQ);
  nand nand_4 (nand_4_out, Q, nand_2_out, nand_2_out);
  and and_2 (nQ, nand_4_out, not_2_out);
  not not_2 (not_2_out, P);
endmodule
