// Logisim project ej3.circ as structural Verilog: 1 circuit, main circuit main
module main (
  input  J,
  input  K,
  input  P,
  input  E,
  input  C,
  output Q,
  output nQ
);

  wire Clk_out;

  Clock Clk (.out(Clk_out));
  J_K_Flip_Flop j_k_ff_1 (.J(J), .clk(Clk_out), .K(K), .Q(Q), .Qn(nQ), .preset(P), .en(E), .reset(C));
endmodule
