// Logisim project ej5.circ as structural Verilog: 1 circuit, main circuit main
module main (
  input  [1:0] Y,
  input  Clk,
  output [1:0] Q,
  output Z0,
  output Z1
);

  wire and_1_out, and_2_out, and_3_out, and_4_out, and_5_out, and_6_out, not_1_out, not_2_out, or_1_out,
       or_2_out, or_3_out;

  not not_1 (not_1_out, Y[1]);
  not not_2 (not_2_out, Q[0]);
  and and_1 (and_1_out, Y[0], Q[1]);
  and and_2 (and_2_out, Q[0], Y[0], not_1_out);
  and and_3 (and_3_out, Y[1], not_2_out);
  or or_1 (or_1_out, Y[1], and_1_out);
  or or_2 (or_2_out, and_2_out, and_3_out);
  J_K_Flip_Flop JK0 (.J(Y[0]), .clk(Clk), .K(or_1_out), .Q(Q[0]));  // open: Qn, preset, en, reset
  J_K_Flip_Flop JK1 (.J(or_2_out), .clk(Clk), .K(Y[0]), .Q(Q[1]));  // open: Qn, preset, en, reset
  and and_4 (and_4_out, Y[1], Q[1]);
  and and_5 (and_5_out, Q[0], Y[1]);
  and and_6 (and_6_out, Q[1], Y[0]);
  or or_3 (or_3_out, and_5_out, and_6_out);
  D_Flip_Flop d_ff_1 (.clk(Clk), .D(and_4_out), .Q(Z0));  // open: Qn, preset, en, reset
  D_Flip_Flop d_ff_2 (.clk(Clk), .D(or_3_out), .Q(Z1));  // open: Qn, preset, en, reset

  // Notes on the sheet:
  //   Cambio
  //   Producto
endmodule
