// Logisim project ejns.circ as structural Verilog: 1 circuit, main circuit main
module main (
  input  in_1,
  input  in_2,
  input  in_3
);

  wire and_1_out, clock_1_out;
  wire [3:0] j_k_ff_4_q;

  Clock clock_1 (.out(clock_1_out));
  J_K_Flip_Flop j_k_ff_1 (
    .J(in_1), .clk(clock_1_out), .K(in_1), .Q(j_k_ff_4_q[3]), .preset(in_2), .reset(and_1_out));  // open: Qn, en
  J_K_Flip_Flop j_k_ff_2 (
    .J(in_1), .clk(j_k_ff_4_q[3]), .K(in_1), .Q(j_k_ff_4_q[2]), .preset(in_2), .reset(and_1_out));  // open: Qn, en
  J_K_Flip_Flop j_k_ff_3 (
    .J(in_1), .clk(j_k_ff_4_q[2]), .K(in_1), .Q(j_k_ff_4_q[1]), .preset(in_2), .reset(and_1_out));  // open: Qn, en
  and and_1 (and_1_out, j_k_ff_4_q[1], j_k_ff_4_q[0], in_3);
  J_K_Flip_Flop j_k_ff_4 (
    .J(in_1), .clk(j_k_ff_4_q[1]), .K(in_1), .Q(j_k_ff_4_q[0]), .preset(in_2), .reset(and_1_out));  // open: Qn, en
  Hex_Digit_Display hex_digit_display_1 (.value(j_k_ff_4_q));  // open: dp
endmodule
