// Logisim project ej1.circ as structural Verilog: 1 circuit, main circuit main
module main (
  input  y,
  input  x,
  input  z,
  output out_4
);

  wire n_x_z_out, not_1_out, not_2_out, not_3_out, nx_ny_out, x_y_out;

  and x_y (x_y_out, x, y);
  not not_1 (not_1_out, y);
  not not_2 (not_2_out, x);
  and n_x_z (n_x_z_out, z, x);
  and nx_ny (nx_ny_out, not_1_out, not_2_out);
  not not_3 (not_3_out, n_x_z_out);
  or or_1 (out_4, x_y_out, x_y_out, nx_ny_out, nx_ny_out, not_3_out);
endmodule
