// Logisim project ej2-original.circ as structural Verilog: 1 circuit, main circuit main
module main (
  input  a,
  input  b,
  input  c,
  input  d,
  output out_5
);

  wire a_nb_out, and_1_out, bd_out, c_bd_out, na_nb_out, not_1_out, not_2_out, or_1_out;

  not not_1 (not_1_out, a);
  not not_2 (not_2_out, b);
  and bd (bd_out, d, b);
  and na_nb (na_nb_out, not_2_out, not_1_out);
  and a_nb (a_nb_out, a, not_2_out);
  or c_bd (c_bd_out, c, bd_out);
  and and_1 (and_1_out, a_nb_out, c_bd_out);
  or or_1 (or_1_out, and_1_out, na_nb_out);
  and and_2 (out_5, or_1_out, c);
endmodule
