// Logisim project ej2-simplificada.circ as structural Verilog: 1 circuit, main circuit main
module main (
  input  b,
  input  c,
  output out_3
);

  wire not_1_out;

  not not_1 (not_1_out, b);
  and nbc (out_3, c, not_1_out);
endmodule
