// Logisim project ej3d-pos.circ as structural Verilog: 1 circuit, main circuit main
module main (
  input  a,
  input  b,
  input  c,
  input  d,
  output x
);

  wire not_1_out, not_2_out, not_3_out, not_4_out, not_5_out, not_6_out, or_1_out, or_2_out, or_3_out;

  not not_1 (not_1_out, c);
  or or_1 (or_1_out, a, not_1_out, not_2_out);
  not not_2 (not_2_out, d);
  not not_3 (not_3_out, b);
  or or_2 (or_2_out, not_3_out, not_4_out, not_5_out);
  not not_4 (not_4_out, c);
  not not_5 (not_5_out, d);
  or or_3 (or_3_out, b, c, not_6_out);
  not not_6 (not_6_out, d);
  and and_1 (x, or_1_out, or_2_out, or_3_out);
endmodule
