// Logisim project ej4c.circ as structural Verilog: 1 circuit, main circuit main
module main (
  input  a,
  input  b,
  input  c,
  input  d,
  output out_5
);

  wire a_nbc_out, ab_ncd_out, na_nc_nd_out, nand_1_out, nand_2_out, nand_3_out, nand_4_out, nand_5_out,
       nand_6_out, nand_7_out, nand_8_out, nand_9_out, nb_nc_nd_out, nbcd_out;

  nand nand_1 (nand_1_out, b, b);
  nand nand_2 (nand_2_out, b, b);
  nand nand_3 (nand_3_out, c, c);
  nand nand_4 (nand_4_out, d, d);
  nand nand_5 (nand_5_out, d, d);
  nand nand_6 (nand_6_out, c, c);
  nand nand_7 (nand_7_out, a, a);
  nand nand_8 (nand_8_out, b, b);
  nand nand_9 (nand_9_out, c, c);
  nand a_nbc (a_nbc_out, a, nand_1_out, c);
  nand nb_nc_nd (nb_nc_nd_out, nand_2_out, nand_3_out, nand_3_out, nand_4_out);
  nand nbcd (nbcd_out, c, nand_8_out, d);
  nand ab_ncd (ab_ncd_out, b, nand_9_out, d, a);
  nand na_nc_nd (na_nc_nd_out, nand_5_out, nand_6_out, nand_7_out);
  nand nand_10 (out_5, a_nbc_out, nb_nc_nd_out, na_nc_nd_out, nbcd_out, ab_ncd_out);
endmodule
