// Logisim project ej5.circ as structural Verilog: 1 circuit, main circuit main
module main (
  input  a,
  input  b,
  input  c,
  input  d,
  input  e,
  output out_6
);

  wire b_nc_nd_out, cd_out, nab_nce_out, nbc_ne_out, nc_nde_out, not_1_out, not_2_out, not_3_out, not_4_out,
       not_5_out;

  not not_1 (not_1_out, a);
  not not_2 (not_2_out, b);
  not not_3 (not_3_out, c);
  not not_4 (not_4_out, d);
  not not_5 (not_5_out, e);
  and nab_nce (nab_nce_out, not_1_out, b, not_3_out, e);
  and nc_nde (nc_nde_out, not_3_out, not_4_out, e);
  and b_nc_nd (b_nc_nd_out, b, not_3_out, not_4_out);
  and nbc_ne (nbc_ne_out, not_2_out, c, not_5_out);
  and cd (cd_out, c, d);
  or or_1 (out_6, nab_nce_out, nc_nde_out, b_nc_nd_out, nbc_ne_out, cd_out);
endmodule
