// Logisim project ej2.circ as structural Verilog: 1 circuit, main circuit main
module main (
  input  a,
  input  b,
  input  c,
  input  d,
  output out_5
);

  wire and_1_out, and_2_out, and_3_out, and_4_out, not_1_out, not_2_out, not_3_out, or_1_out, or_2_out;

  and and_1 (and_1_out, b, d);
  not not_1 (not_1_out, a);
  not not_2 (not_2_out, b);
  not not_3 (not_3_out, b);
  or or_1 (or_1_out, c, and_1_out);
  and and_2 (and_2_out, not_1_out, not_2_out);
  and and_3 (and_3_out, a, not_3_out);
  and and_4 (and_4_out, and_3_out, or_1_out);
  or or_2 (or_2_out, and_4_out, and_2_out);
  and and_5 (out_5, or_2_out, c);
endmodule
