// Logisim project ej3d.circ as structural Verilog: 1 circuit, main circuit main
module main (
  input  c,
  input  b,
  input  d,
  output out_4
);

  wire not_1_out, not_2_out, not_3_out;

  not not_1 (not_1_out, c);
  not not_2 (not_2_out, b);
  not not_3 (not_3_out, d);
  or or_1 (out_4, not_1_out, not_2_out, not_3_out);
endmodule
