// Logisim project ej4b.circ as structural Verilog: 1 circuit, main circuit main
module main (
  input  a,
  input  b,
  input  c,
  input  d,
  output out_5
);

  wire a_nbc_out, ab_ncd_out, na_nc_nd_out, nb_nc_nd_out, nbcd_out, not_1_out, not_2_out;

  not not_1 (not_1_out, b);
  not not_2 (not_2_out, c);
  and a_nbc (a_nbc_out, a, c, not_1_out);
  and nbcd (nbcd_out, not_1_out, c, d);
  and ab_ncd (ab_ncd_out, b, d, not_2_out, a);
  nor na_nc_nd (na_nc_nd_out, a, c, d);
  nor nb_nc_nd (nb_nc_nd_out, b, c, d);
  or or_1 (out_5, na_nc_nd_out, nb_nc_nd_out, a_nbc_out, nbcd_out, ab_ncd_out);
endmodule
